# Fritzing sketch Schematics (saved by Fritzing 0.9.2b)
breadboards: 1

parts:
  Bauteil1 = Arduino Uno (Rev3)
  R1 = Resistor [tolerance=±5% resistance=220 package=THT]
  R2 = Resistor [tolerance=±5% resistance=220 package=THT]

nets:
  N1: Bauteil1.A1, R1.Pin_0, R2.Pin_1
  N2: Bauteil1.GND, R2.Pin_0

notes:
  2S Lipo
  "normal output" "balancer connection"
